// Digital circuit main.dig as structural Verilog
module main (
  input  Clock,
  output [5:0] FUNCT,
  output [5:0] out_3,
  output [31:0] out_4,
  output [31:0] out_5
);

  wire AC, ALU_SRC, ex_mem_1_o_mr, ex_mem_1_o_mtr, ex_mem_1_o_mw, ex_mem_1_o_rw, id_ex_1_o_alus,
       id_ex_1_o_mr, id_ex_1_o_mtr, id_ex_1_o_mw, id_ex_1_o_rw, MEM_TO_REG, mem_wb_1_o_mtr, mem_wb_1_o_rw,
       MR, RgD, RW, Write_MEM;
  wire [1:0] AO, id_ex_1_o_ao;
  wire [4:0] ex_mem_1_o_dest, id_ex_part_2_1_o_rgd_1, id_ex_part_2_1_o_rgd_2, multiplexer_1_out,
       multiplexer_2_out;
  wire [31:0] _32x32_1_r_d1, _32x32_1_r_d2, add_1_s, bitextender_1_out, ex_mem_1_o_r2, ex_mem_1_o_result,
       id_ex_1_o_r1, id_ex_1_o_r2, id_ex_1_o_s32, mem_wb_1_o_alu_res, mem_wb_1_o_read_d, memory_24x32_1_data,
       multiplexer_3_out, pc_1_pc_out, R31, ula_1_p5, WB;

  PC pc_1 (.Clok(Clock), .PC_IN(add_1_s), .PC_OUT(pc_1_pc_out));
  Add #(.Bits(32)) add_1 (.a(pc_1_pc_out), .b(32'h4), .c_i(1'b0), .s(add_1_s));  // open: c_o
  instruction_mem instruction_mem_1 (._32__ADDR(pc_1_pc_out), ._1__Enable(Clock), ._32__Out(out_5));
  IF_ID if_id_1 (.In(out_5), .Clk(Clock), .Out({out_3, out_4[25:6], FUNCT}));
  Control control_1 (
    .RgD(RgD), .AluS(ALU_SRC), .MTR(MEM_TO_REG), .RW(RW), .MR(MR), .MW(Write_MEM), .AO_1(AO[0]),
    .AO_0(AO[1]), .Clk(Clock), .Op(out_3));  // open: B, J, APC
  Multiplexer #(.Bits(5)) multiplexer_1 (.sel(RgD), .in_0(out_4[20:16]), .in_1(out_4[15:11]), .out(multiplexer_1_out));
  _32x32 _32x32_1 (
    ._32_W_d(WB), ._5__R_reg1(out_4[25:21]), ._5__R_reg2(out_4[20:16]), ._5b__A_set(multiplexer_1_out),
    .Clk(Clock), ._1__W_e(mem_wb_1_o_rw), .R_d1(_32x32_1_r_d1), .R_d2(_32x32_1_r_d2), .R31(R31));
  BitExtender #(.inputBits(16), .outputBits(32)) bitextender_1 (.in({out_4[15:6], FUNCT}), .out(bitextender_1_out));
  ID_EX id_ex_1 (
    .RW(RW), .MR(MR), .MW(Write_MEM), .MTR(MEM_TO_REG), .RgD(RgD), .AluS(ALU_SRC), .AO(AO),
    .R_1(_32x32_1_r_d1), .R_2(_32x32_1_r_d2), .S_32(bitextender_1_out), .Clk(Clock), .O_RW(id_ex_1_o_rw),
    .O_MR(id_ex_1_o_mr), .O_MW(id_ex_1_o_mw), .O_MTR(id_ex_1_o_mtr), .O_AluS(id_ex_1_o_alus),
    .O_AO(id_ex_1_o_ao), .O_R1(id_ex_1_o_r1), .O_R2(id_ex_1_o_r2), .O_S32(id_ex_1_o_s32));  // open: O_RgD
  ID_EX_part_2 id_ex_part_2_1 (
    .Clk(Clock), .RgD_1(out_4[20:16]), .RgD_2(out_4[15:11]), .O_RgD_1(id_ex_part_2_1_o_rgd_1),
    .O_RgD_2(id_ex_part_2_1_o_rgd_2));
  Multiplexer #(.Bits(5)) multiplexer_2 (
    .sel(RgD), .in_0(id_ex_part_2_1_o_rgd_1), .in_1(id_ex_part_2_1_o_rgd_2), .out(multiplexer_2_out));
  Seven_Seg_Hex seven_seg_hex_1 (.d(R31[19:16]), .dp(1'b0));
  Seven_Seg_Hex seven_seg_hex_2 (.d(R31[15:12]), .dp(1'b0));
  Multiplexer #(.Bits(32)) multiplexer_3 (
    .sel(id_ex_1_o_alus), .in_0(id_ex_1_o_r2), .in_1(id_ex_1_o_s32), .out(multiplexer_3_out));
  // ALU_Control alu_control_1: pin names not known; wires that end beside it: id_ex_1_o_ao[0], id_ex_1_o_ao[1], FUNCT, AC
  Seven_Seg_Hex seven_seg_hex_3 (.d(R31[11:8]), .dp(1'b0));
  Seven_Seg_Hex seven_seg_hex_4 (.d(R31[7:4]), .dp(1'b0));
  // ula ula_1: pin names not known; wires that end beside it: AC, id_ex_1_o_r1, multiplexer_3_out, {6{1'b0}}, ula_1_p5
  Seven_Seg_Hex seven_seg_hex_5 (.d(R31[3:0]), .dp(1'b0));
  EX_MEM ex_mem_1 (
    .RW(id_ex_1_o_rw), .MR(id_ex_1_o_mr), .MW(id_ex_1_o_mw), .MTR(id_ex_1_o_mtr), .Result(ula_1_p5),
    .R_2(id_ex_1_o_r2), .Dest(multiplexer_2_out), .Clk(Clock), .O_RW(ex_mem_1_o_rw), .O_MR(ex_mem_1_o_mr),
    .O_MW(ex_mem_1_o_mw), .O_MTR(ex_mem_1_o_mtr), .O_Result(ex_mem_1_o_result), .O_R2(ex_mem_1_o_r2),
    .O_Dest(ex_mem_1_o_dest));
  memory_24x32 memory_24x32_1 (
    .address(ex_mem_1_o_result[23:0]), .write_data(ex_mem_1_o_r2), .mem_write(ex_mem_1_o_mw), .clock(Clock),
    .mem_read(ex_mem_1_o_mr), .data(memory_24x32_1_data));
  MEM_WB mem_wb_1 (
    .RW(ex_mem_1_o_rw), .MTR(ex_mem_1_o_mtr), .Read_D(memory_24x32_1_data), .Alu_res(ex_mem_1_o_result),
    .Dest(ex_mem_1_o_dest), .Clk(Clock), .O_RW(mem_wb_1_o_rw), .O_MTR(mem_wb_1_o_mtr),
    .O_Read_D(mem_wb_1_o_read_d), .O_Alu_res(mem_wb_1_o_alu_res));  // open: O_Dest
  Multiplexer #(.Bits(32)) multiplexer_4 (
    .sel(mem_wb_1_o_mtr), .in_0(mem_wb_1_o_alu_res), .in_1(mem_wb_1_o_read_d), .out(WB));

  assign {out_4[31:26], out_4[5:0]} = {out_3, FUNCT};

  // Other names for the same wires on the sheet: OPCODE[5:0] = out_3

  // Notes on the sheet:
  //   Instruções na memória
  //   Nop
  //   Nop
  //   ADDI $S0, $S0, 5
  //   ADD $RA, $S0, $S0
  //   ADDI $RA, $RA, 5
  //   ADDI $RA, $RA, 5
  //   ADDI $RA, $RA, 5
  //   ADDI $RA, $RA, 5
  //   ADDI $RA, $RA, 5
  //   $S0 = 16, hex = 10
  //   $RA = 31, hex = 1F
  //   00000000
  //   00000000
  //   22100005
  //   0210f820
  //   23ff0005
  //   23ff0005
  //   23ff0005
  //   23ff0005
  //   23ff0005
  //   Instrução [15-0]
  //   Instrução [20-16]
  //   Instrução [15-11]
  //   AluOP
endmodule
